# Fritzing sketch sistan proyek (saved by Fritzing 0.9.3b)
breadboards: 1

parts:
  PIR1 = PIR sensor
  Part1 = Arduino Uno (Rev3)
  DHT1 = DHT22 Humidity and Temperature Sensor
  U1 = 2-Channel 5v Relay Shield [package=relay-2ch5v10a]
  e-radionica_com1 = LM393 LDR breakout [part_number=100027]
  R1 = Resistor [tolerance=±5% resistance=220 package="0603 [SMD]"]
  R2 = Resistor [tolerance=±5% resistance=220 package="0805 [SMD]"]
  R3 = Resistor [tolerance=±5% resistance=220 package="1206 [SMD]"]
  LED2 = LEDs [package=led10mm]
  LED4 = smd LED [color="Green (570nm)" package="0603 [SMD]"]
  LED5 = smd LED [color="Red (633nm)" package="0603 [SMD]"]
  LED6 = smd LED [color="Yellow (595nm)" package="0603 [SMD]"]
  JACK1 = 2.1mm Barrel Jack with Terminal Block
  LED7 = LEDs [package=led10mm]
  JACK2 = 2.1mm Barrel Jack with Terminal Block
  J1 = Piezo Speaker

nets:
  VDD: PIR1.VDD, Part1.5V, DHT1.VDD, U1.VCC, e-radionica_com1.VCC, J1.pin2
  N1: PIR1.SIG, Part1.A1
  GND: PIR1.GND, Part1.GND, DHT1.GND, U1.GND, e-radionica_com1.GND, R1.Pin_1, R2.Pin_1, R3.Pin_1
  N2: Part1.A0, e-radionica_com1.AO
  N3: Part1.D8, J1.pin1
  N4: Part1.D2, DHT1.DATA
  N5: Part1.D3_PWM, LED5.cathode
  N6: Part1.D4, LED6.cathode
  N7: Part1.D5_PWM, LED4.cathode
  N8: Part1.D6_PWM, U1.IN2
  N9: Part1.D7, U1.IN1
  N10: U1.K1-In, JACK2.NEG
  N11: U1.K1-On, LED2.C
  N12: U1.K2-In, JACK1.POS
  N13: U1.K2-On, LED7.C
  N14: R1.Pin_0, LED4.anode
  N15: R2.Pin_0, LED6.anode
  N16: R3.Pin_0, LED5.anode
  N17: LED2.A, JACK2.POS
  N18: JACK1.NEG, LED7.A

notes:
  Buzzer
  Arduino Uno
  Pir
  LDR
  Lampu
  Relay
  Steker
  LED
  DHT 22
  Kelompok 07
  Andreas Arta P.M
  Nova Sirait
  Joe A.W. Manurung
  Sulastri Silalahi

custom parts:
  2-Channel 5v Relay Shield: 2 Channel 5v Relay Shield w. 2x SPD-06VDC-SD-C
  LEDs: LEDs Standard schematic elements and footprints for 5mm, 3mm, 1206, and 0603 sized LEDs. 5mm - Spark Fun Electronics SKU : COM-00529 (and others)
